// Logisim project Final_32bit.circ as structural Verilog: 13 circuits, main circuit main
module main (
  input  Reset
);

  wire alu_1_math_error, clk, DWE, WE;
  wire [1:0] Data_selector;
  wire [2:0] ALU_opp;
  wire [3:0] Opcode;
  wire [6:0] writer_1_data_out;
  wire [7:0] Read_A, Read_B, WAddr;
  wire [23:0] count_1_counter_out;
  wire [31:0] alu_1_alu_out, multiplexer_1_out, register_32data_8address_1_a_out,
       register_32data_8address_1_b_out;
  wire [31:16] rom_1_data;

  Clock clock_1 (.out(clk));
  Count count_1 (.Reset(Reset), .clk(clk), .Counter_out(count_1_counter_out));
  ROM #(.addrWidth(24), .dataWidth(44)) rom_1 (
    .addr(count_1_counter_out), .data({Opcode, WAddr, rom_1_data, Read_B, Read_A}));
  ROM #(.addrWidth(4), .dataWidth(7)) rom_2 (.addr(Opcode), .data({ALU_opp, Data_selector, DWE, WE}));
  // Probe on multiplexer_1_out
  Multiplexer #(.select(2), .width(32)) multiplexer_1 (
    .in0({rom_1_data, Read_B, Read_A}), .in1(alu_1_alu_out), .in2(register_32data_8address_1_a_out),
    .out(multiplexer_1_out), .sel(Data_selector));  // open: in3
  // Probe on WAddr
  // Probe on Data_selector
  // Probe on ALU_opp
  // Probe on Read_A
  Register_32Data_8Address register_32data_8address_1 (
    .CLK(clk), .WE(WE), .Data_in(multiplexer_1_out), .Address(WAddr), .Read_B(Read_B), .Read_A(Read_A),
    .A_out(register_32data_8address_1_a_out), .B_out(register_32data_8address_1_b_out));
  // Probe on Read_B
  // Probe on register_32data_8address_1_a_out
  // Probe on register_32data_8address_1_b_out
  ALU alu_1 (
    .S(ALU_opp), .A(register_32data_8address_1_a_out), .B(register_32data_8address_1_b_out),
    .ALU_out(alu_1_alu_out), .Math_Error(alu_1_math_error));
  // RGBLED rgbled_1: pin names not known; wires that end beside it: alu_1_math_error, alu_1_math_error
  // Probe on alu_1_alu_out
  Writer writer_1 (.Data_in(register_32data_8address_1_a_out), .Decode(ALU_opp), .Data_out(writer_1_data_out));
  // Probe on writer_1_data_out
  TTY tty_1 (.data(writer_1_data_out), .clk(clk), .we(DWE), .clr(Reset));

  // Notes on the sheet:
  //   contents of rom_1 (hex, n*v repeats v):
  //   0 1ff0000004a 10100000075 10200000073 10300000074 11800000069 1050000006e 300000000ff 30000000001
  //   30000000002 30000000003 30000000018 30000000005 11a00000020 3000000001a 10100000048 10200000075
  //   10300000074 11800000063 10500000068 10600000065 1070000006e 10800000073 30000000001 30000000002
  //   30000000003 30000000018 30000000005 30000000006 30000000007 30000000008 10200000023 10900000004
  //   10b00000002 3000000001a 30000000002 b0000000009 b000000000b 1010000000a 30000000001 1020000002b
  //   1030000003d 1180000002d 10a00000005 b000000000a 30000000002 b000000000b 30000000003 70c00000b0a
  //   b000000000c 30000000001 b000000000a 30000000018 b000000000b 30000000003 1ff00000001 a0d00000b0b
  //   70e0000ff0d 70f00000e0a b000000000f 30000000001 b000000000a 30000000018 b000000000b 30000000003
  //   f1d00000b0a b000000001d 30000000001 11e00000043 11f0000006f 12000000070 12100000079 1220000003a
  //   3000000001e 3000000001f 30000000020 30000000021 30000000022 2230000001d 3000000001a b0000000023
  //   contents of rom_2 (hex, n*v repeats v):
  //   0 1 9 2 5 15 25 35 45 55 65 12 0 0 0 75
  //   Error
  //   Light
endmodule

module Register_32Bit (
  input  [31:0] Data_in,
  input  Set,
  output [31:0] out_3
);

  wire undriven, undriven_2, undriven_3, undriven_4, undriven_5, undriven_6, undriven_7, undriven_8,
       undriven_9, undriven_10, undriven_11, undriven_12, undriven_13, undriven_14, undriven_15, undriven_16,
       undriven_17, undriven_18, undriven_19, undriven_20, undriven_21, undriven_22, undriven_23,
       undriven_24, undriven_25, undriven_26, undriven_27, undriven_28;

  D_Flip_Flop d_ff_1 (.D(Data_in[24]), .clk(Set), .Q(out_3[24]), .reset(undriven));  // open: Qn, preset
  D_Flip_Flop d_ff_2 (.D(Data_in[25]), .clk(Set), .Q(out_3[25]), .preset(undriven), .reset(undriven_2));  // open: Qn
  D_Flip_Flop d_ff_3 (.D(Data_in[26]), .clk(Set), .Q(out_3[26]), .preset(undriven_2), .reset(undriven_3));  // open: Qn
  D_Flip_Flop d_ff_4 (.D(Data_in[27]), .clk(Set), .Q(out_3[27]), .preset(undriven_3), .reset(undriven_4));  // open: Qn
  D_Flip_Flop d_ff_5 (.D(Data_in[28]), .clk(Set), .Q(out_3[28]), .preset(undriven_4), .reset(undriven_5));  // open: Qn
  D_Flip_Flop d_ff_6 (.D(Data_in[29]), .clk(Set), .Q(out_3[29]), .preset(undriven_5), .reset(undriven_6));  // open: Qn
  D_Flip_Flop d_ff_7 (.D(Data_in[30]), .clk(Set), .Q(out_3[30]), .preset(undriven_6), .reset(undriven_7));  // open: Qn
  D_Flip_Flop d_ff_8 (.D(Data_in[31]), .clk(Set), .Q(out_3[31]), .preset(undriven_7));  // open: Qn, reset
  D_Flip_Flop d_ff_9 (.D(Data_in[16]), .clk(Set), .Q(out_3[16]), .reset(undriven_8));  // open: Qn, preset
  D_Flip_Flop d_ff_10 (.D(Data_in[17]), .clk(Set), .Q(out_3[17]), .preset(undriven_8), .reset(undriven_9));  // open: Qn
  D_Flip_Flop d_ff_11 (
    .D(Data_in[18]), .clk(Set), .Q(out_3[18]), .preset(undriven_9), .reset(undriven_10));  // open: Qn
  D_Flip_Flop d_ff_12 (
    .D(Data_in[19]), .clk(Set), .Q(out_3[19]), .preset(undriven_10), .reset(undriven_11));  // open: Qn
  D_Flip_Flop d_ff_13 (
    .D(Data_in[20]), .clk(Set), .Q(out_3[20]), .preset(undriven_11), .reset(undriven_12));  // open: Qn
  D_Flip_Flop d_ff_14 (
    .D(Data_in[21]), .clk(Set), .Q(out_3[21]), .preset(undriven_12), .reset(undriven_13));  // open: Qn
  D_Flip_Flop d_ff_15 (
    .D(Data_in[22]), .clk(Set), .Q(out_3[22]), .preset(undriven_13), .reset(undriven_14));  // open: Qn
  D_Flip_Flop d_ff_16 (.D(Data_in[23]), .clk(Set), .Q(out_3[23]), .preset(undriven_14));  // open: Qn, reset
  D_Flip_Flop d_ff_17 (.D(Data_in[8]), .clk(Set), .Q(out_3[8]), .reset(undriven_15));  // open: Qn, preset
  D_Flip_Flop d_ff_18 (.D(Data_in[9]), .clk(Set), .Q(out_3[9]), .preset(undriven_15), .reset(undriven_16));  // open: Qn
  D_Flip_Flop d_ff_19 (
    .D(Data_in[10]), .clk(Set), .Q(out_3[10]), .preset(undriven_16), .reset(undriven_17));  // open: Qn
  D_Flip_Flop d_ff_20 (
    .D(Data_in[11]), .clk(Set), .Q(out_3[11]), .preset(undriven_17), .reset(undriven_18));  // open: Qn
  D_Flip_Flop d_ff_21 (
    .D(Data_in[12]), .clk(Set), .Q(out_3[12]), .preset(undriven_18), .reset(undriven_19));  // open: Qn
  D_Flip_Flop d_ff_22 (
    .D(Data_in[13]), .clk(Set), .Q(out_3[13]), .preset(undriven_19), .reset(undriven_20));  // open: Qn
  D_Flip_Flop d_ff_23 (
    .D(Data_in[14]), .clk(Set), .Q(out_3[14]), .preset(undriven_20), .reset(undriven_21));  // open: Qn
  D_Flip_Flop d_ff_24 (.D(Data_in[15]), .clk(Set), .Q(out_3[15]), .preset(undriven_21));  // open: Qn, reset
  D_Flip_Flop d_ff_25 (.D(Data_in[0]), .clk(Set), .Q(out_3[0]), .reset(undriven_22));  // open: Qn, preset
  D_Flip_Flop d_ff_26 (.D(Data_in[1]), .clk(Set), .Q(out_3[1]), .preset(undriven_22), .reset(undriven_23));  // open: Qn
  D_Flip_Flop d_ff_27 (.D(Data_in[2]), .clk(Set), .Q(out_3[2]), .preset(undriven_23), .reset(undriven_24));  // open: Qn
  D_Flip_Flop d_ff_28 (.D(Data_in[3]), .clk(Set), .Q(out_3[3]), .preset(undriven_24), .reset(undriven_25));  // open: Qn
  D_Flip_Flop d_ff_29 (.D(Data_in[4]), .clk(Set), .Q(out_3[4]), .preset(undriven_25), .reset(undriven_26));  // open: Qn
  D_Flip_Flop d_ff_30 (.D(Data_in[5]), .clk(Set), .Q(out_3[5]), .preset(undriven_26), .reset(undriven_27));  // open: Qn
  D_Flip_Flop d_ff_31 (.D(Data_in[6]), .clk(Set), .Q(out_3[6]), .preset(undriven_27), .reset(undriven_28));  // open: Qn
  D_Flip_Flop d_ff_32 (.D(Data_in[7]), .clk(Set), .Q(out_3[7]), .preset(undriven_28));  // open: Qn, reset
endmodule

module Register_32Data_8Address (
  input  [7:0] Read_A,
  input  [31:0] Data_in,
  input  CLK,
  input  WE,
  input  [7:0] Address,
  input  [7:0] Read_B,
  output [31:0] A_out,
  output [31:0] B_out
);

  wire and_1_out;
  wire [3:0] decoder_1_out0;
  wire [31:0] register_32data_6address_1_a_out, register_32data_6address_1_b_out,
       register_32data_6address_2_a_out, register_32data_6address_2_b_out, register_32data_6address_3_a_out,
       register_32data_6address_3_b_out, register_32data_6address_4_a_out, register_32data_6address_4_b_out;

  Decoder #(.select(2)) decoder_1 (
    .out0(decoder_1_out0[0]), .out1(decoder_1_out0[1]), .out2(decoder_1_out0[2]), .out3(decoder_1_out0[3]),
    .sel(Address[7:6]), .en(and_1_out));
  and and_1 (and_1_out, CLK, WE);
  Register_32Data_6Address register_32data_6address_1 (
    .Data_in(Data_in), .WE(decoder_1_out0[0]), .Address(Address[5:0]), .Read_B(Read_B[5:0]),
    .Read_A(Read_A[5:0]), .A_out(register_32data_6address_1_a_out), .B_out(register_32data_6address_1_b_out));
  Register_32Data_6Address register_32data_6address_2 (
    .Data_in(Data_in), .WE(decoder_1_out0[1]), .Address(Address[5:0]), .Read_B(Read_B[5:0]),
    .Read_A(Read_A[5:0]), .A_out(register_32data_6address_2_a_out), .B_out(register_32data_6address_2_b_out));
  Register_32Data_6Address register_32data_6address_3 (
    .Data_in(Data_in), .WE(decoder_1_out0[2]), .Address(Address[5:0]), .Read_B(Read_B[5:0]),
    .Read_A(Read_A[5:0]), .A_out(register_32data_6address_3_a_out), .B_out(register_32data_6address_3_b_out));
  Register_32Data_6Address register_32data_6address_4 (
    .Data_in(Data_in), .WE(decoder_1_out0[3]), .Address(Address[5:0]), .Read_B(Read_B[5:0]),
    .Read_A(Read_A[5:0]), .A_out(register_32data_6address_4_a_out), .B_out(register_32data_6address_4_b_out));
  Multiplexer #(.select(2), .width(32)) multiplexer_1 (
    .in0(register_32data_6address_1_a_out), .in1(register_32data_6address_2_a_out),
    .in2(register_32data_6address_3_a_out), .in3(register_32data_6address_4_a_out), .out(A_out),
    .sel(Read_A[7:6]));
  Multiplexer #(.select(2), .width(32)) multiplexer_2 (
    .in0(register_32data_6address_1_b_out), .in1(register_32data_6address_2_b_out),
    .in2(register_32data_6address_3_b_out), .in3(register_32data_6address_4_b_out), .out(B_out),
    .sel(Read_B[7:6]));

  // Other names for the same wires on the sheet: Addr[5:0] = Address[5:0]
endmodule

module Register_32Data_4Address (
  input  [3:0] Read_A,
  input  [31:0] Data_in,
  input  WE,
  input  [3:0] Address,
  input  [3:0] Read_B,
  output [31:0] A_out,
  output [31:0] B_out
);

  wire [3:0] decoder_1_out0;
  wire [31:0] register_32data_2address_1_a_out, register_32data_2address_1_b_out,
       register_32data_2address_2_a_out, register_32data_2address_2_b_out, register_32data_2address_3_a_out,
       register_32data_2address_3_b_out, register_32data_2address_4_a_out, register_32data_2address_4_b_out;

  Decoder #(.select(2)) decoder_1 (
    .out0(decoder_1_out0[0]), .out1(decoder_1_out0[1]), .out2(decoder_1_out0[2]), .out3(decoder_1_out0[3]),
    .sel(Address[3:2]), .en(WE));
  Register_32Data_2Address register_32data_2address_1 (
    .Data_in(Data_in), .WE(decoder_1_out0[0]), .Address(Address[1:0]), .Read_B(Read_B[1:0]),
    .Read_A(Read_A[1:0]), .A_out(register_32data_2address_1_a_out), .B_out(register_32data_2address_1_b_out));
  Register_32Data_2Address register_32data_2address_2 (
    .Data_in(Data_in), .WE(decoder_1_out0[1]), .Address(Address[1:0]), .Read_B(Read_B[1:0]),
    .Read_A(Read_A[1:0]), .A_out(register_32data_2address_2_a_out), .B_out(register_32data_2address_2_b_out));
  Register_32Data_2Address register_32data_2address_3 (
    .Data_in(Data_in), .WE(decoder_1_out0[2]), .Address(Address[1:0]), .Read_B(Read_B[1:0]),
    .Read_A(Read_A[1:0]), .A_out(register_32data_2address_3_a_out), .B_out(register_32data_2address_3_b_out));
  Register_32Data_2Address register_32data_2address_4 (
    .Data_in(Data_in), .WE(decoder_1_out0[3]), .Address(Address[1:0]), .Read_B(Read_B[1:0]),
    .Read_A(Read_A[1:0]), .A_out(register_32data_2address_4_a_out), .B_out(register_32data_2address_4_b_out));
  Multiplexer #(.select(2), .width(32)) multiplexer_1 (
    .in0(register_32data_2address_1_a_out), .in1(register_32data_2address_2_a_out),
    .in2(register_32data_2address_3_a_out), .in3(register_32data_2address_4_a_out), .out(A_out),
    .sel(Read_A[3:2]));
  Multiplexer #(.select(2), .width(32)) multiplexer_2 (
    .in0(register_32data_2address_1_b_out), .in1(register_32data_2address_2_b_out),
    .in2(register_32data_2address_3_b_out), .in3(register_32data_2address_4_b_out), .out(B_out),
    .sel(Read_B[3:2]));

  // Other names for the same wires on the sheet: Addr[1:0] = Address[1:0]
endmodule

module Register_32Data_2Address (
  input  [1:0] Read_A,
  input  [31:0] Data_in,
  input  WE,
  input  [1:0] Address,
  input  [1:0] Read_B,
  output [31:0] A_out,
  output [31:0] B_out
);

  wire [3:0] decoder_1_out0;
  wire [31:0] register_32bit_1_out_3, register_32bit_2_out_3, register_32bit_3_out_3, register_32bit_4_out_3;

  Decoder #(.select(2)) decoder_1 (
    .out0(decoder_1_out0[0]), .out1(decoder_1_out0[1]), .out2(decoder_1_out0[2]), .out3(decoder_1_out0[3]),
    .sel(Address), .en(WE));
  Register_32Bit register_32bit_1 (.Data_in(Data_in), .Set(decoder_1_out0[0]), .out_3(register_32bit_1_out_3));
  // Probe on register_32bit_2_out_3
  Register_32Bit register_32bit_2 (.Data_in(Data_in), .Set(decoder_1_out0[1]), .out_3(register_32bit_2_out_3));
  // Probe on register_32bit_3_out_3
  Register_32Bit register_32bit_3 (.Data_in(Data_in), .Set(decoder_1_out0[2]), .out_3(register_32bit_3_out_3));
  // Probe on register_32bit_4_out_3
  Register_32Bit register_32bit_4 (.Data_in(Data_in), .Set(decoder_1_out0[3]), .out_3(register_32bit_4_out_3));
  // Probe on register_32bit_1_out_3
  Multiplexer #(.select(2), .width(32)) multiplexer_1 (
    .in0(register_32bit_1_out_3), .in1(register_32bit_2_out_3), .in2(register_32bit_3_out_3),
    .in3(register_32bit_4_out_3), .out(A_out), .sel(Read_A));
  Multiplexer #(.select(2), .width(32)) multiplexer_2 (
    .in0(register_32bit_1_out_3), .in1(register_32bit_2_out_3), .in2(register_32bit_3_out_3),
    .in3(register_32bit_4_out_3), .out(B_out), .sel(Read_B));
endmodule

module Register_32Data_6Address (
  input  [5:0] Read_A,
  input  [31:0] Data_in,
  input  WE,
  input  [5:0] Address,
  input  [5:0] Read_B,
  output [31:0] A_out,
  output [31:0] B_out
);

  wire [3:0] decoder_1_out0;
  wire [31:0] register_32data_4address_1_a_out, register_32data_4address_1_b_out,
       register_32data_4address_2_a_out, register_32data_4address_2_b_out, register_32data_4address_3_a_out,
       register_32data_4address_3_b_out, register_32data_4address_4_a_out, register_32data_4address_4_b_out;

  Decoder #(.select(2)) decoder_1 (
    .out0(decoder_1_out0[0]), .out1(decoder_1_out0[1]), .out2(decoder_1_out0[2]), .out3(decoder_1_out0[3]),
    .sel(Address[5:4]), .en(WE));
  Register_32Data_4Address register_32data_4address_1 (
    .Data_in(Data_in), .WE(decoder_1_out0[0]), .Address(Address[3:0]), .Read_B(Read_B[3:0]),
    .Read_A(Read_A[3:0]), .A_out(register_32data_4address_1_a_out), .B_out(register_32data_4address_1_b_out));
  Register_32Data_4Address register_32data_4address_2 (
    .Data_in(Data_in), .WE(decoder_1_out0[1]), .Address(Address[3:0]), .Read_B(Read_B[3:0]),
    .Read_A(Read_A[3:0]), .A_out(register_32data_4address_2_a_out), .B_out(register_32data_4address_2_b_out));
  Register_32Data_4Address register_32data_4address_3 (
    .Data_in(Data_in), .WE(decoder_1_out0[2]), .Address(Address[3:0]), .Read_B(Read_B[3:0]),
    .Read_A(Read_A[3:0]), .A_out(register_32data_4address_3_a_out), .B_out(register_32data_4address_3_b_out));
  Register_32Data_4Address register_32data_4address_4 (
    .Data_in(Data_in), .WE(decoder_1_out0[3]), .Address(Address[3:0]), .Read_B(Read_B[3:0]),
    .Read_A(Read_A[3:0]), .A_out(register_32data_4address_4_a_out), .B_out(register_32data_4address_4_b_out));
  // Probe on Read_B[5:4]
  Multiplexer #(.select(2), .width(32)) multiplexer_1 (
    .in0(register_32data_4address_1_a_out), .in1(register_32data_4address_2_a_out),
    .in2(register_32data_4address_3_a_out), .in3(register_32data_4address_4_a_out), .out(A_out),
    .sel(Read_A[5:4]));
  Multiplexer #(.select(2), .width(32)) multiplexer_2 (
    .in0(register_32data_4address_1_b_out), .in1(register_32data_4address_2_b_out),
    .in2(register_32data_4address_3_b_out), .in3(register_32data_4address_4_b_out), .out(B_out),
    .sel(Read_B[5:4]));

  // Other names for the same wires on the sheet: Addr[3:0] = Address[3:0]
endmodule

module ALU (
  input  [31:0] A,
  input  [31:0] B,
  input  [2:0] S,
  output [31:0] ALU_out,
  output Math_Error
);

  wire [31:0] add_32_1_sum, and_1_out, nand_1_out, nor_1_out, or_1_out, xnor_1_out, xor_1_out;

  Add_32 add_32_1 (.A(A), .B(B), .SUB(S[2]), .Carry_Out(Math_Error), .Sum(add_32_1_sum));
  assign or_1_out = A | B;  // OR_Gate or_1, 32 bits wide
  assign xor_1_out = A ^ B;  // XOR_Gate xor_1, 32 bits wide
  assign and_1_out = B & A;  // AND_Gate and_1, 32 bits wide
  assign xnor_1_out = ~(A ^ B);  // XNOR_Gate xnor_1, 32 bits wide
  assign nand_1_out = ~(B & A);  // NAND_Gate nand_1, 32 bits wide
  assign nor_1_out = ~(B | A);  // NOR_Gate nor_1, 32 bits wide
  Multiplexer #(.select(3), .width(32)) multiplexer_1 (
    .in0(xor_1_out), .in1(and_1_out), .in2(or_1_out), .in3(add_32_1_sum), .in4(xnor_1_out), .in5(nand_1_out),
    .in6(nor_1_out), .in7(add_32_1_sum), .out(ALU_out), .sel(S));
endmodule

module Full_Adder (
  input  A,
  input  B,
  input  C,
  output Sum,
  output Carry
);

  wire and_1_out, and_2_out, and_3_out;

  xor xor_1 (Sum, A, B, C);
  and and_1 (and_1_out, A, B);
  and and_2 (and_2_out, A, C);
  and and_3 (and_3_out, B, C);
  or or_1 (Carry, and_1_out, and_2_out, and_3_out);
endmodule

module Add_8 (
  input  [7:0] A,
  input  Carry_in,
  input  [7:0] B,
  output [7:0] Sum,
  output Carry_Out
);

  wire full_adder_1_carry, full_adder_2_carry, full_adder_3_carry, full_adder_4_carry, full_adder_5_carry,
       full_adder_6_carry, full_adder_7_carry;

  Full_Adder full_adder_1 (.A(A[0]), .B(B[0]), .C(Carry_in), .Sum(Sum[0]), .Carry(full_adder_1_carry));
  Full_Adder full_adder_2 (.A(A[1]), .B(B[1]), .C(full_adder_1_carry), .Sum(Sum[1]), .Carry(full_adder_2_carry));
  Full_Adder full_adder_3 (.A(A[2]), .B(B[2]), .C(full_adder_2_carry), .Sum(Sum[2]), .Carry(full_adder_3_carry));
  Full_Adder full_adder_4 (.A(A[3]), .B(B[3]), .C(full_adder_3_carry), .Sum(Sum[3]), .Carry(full_adder_4_carry));
  Full_Adder full_adder_5 (.A(A[4]), .B(B[4]), .C(full_adder_4_carry), .Sum(Sum[4]), .Carry(full_adder_5_carry));
  Full_Adder full_adder_6 (.A(A[5]), .B(B[5]), .C(full_adder_5_carry), .Sum(Sum[5]), .Carry(full_adder_6_carry));
  Full_Adder full_adder_7 (.A(A[6]), .B(B[6]), .C(full_adder_6_carry), .Sum(Sum[6]), .Carry(full_adder_7_carry));
  Full_Adder full_adder_8 (.A(A[7]), .B(B[7]), .C(full_adder_7_carry), .Sum(Sum[7]), .Carry(Carry_Out));
endmodule

module Add_32 (
  input  SUB,
  input  [31:0] A,
  input  [31:0] B,
  output [31:0] Sum,
  output Carry_Out
);

  wire add_8_1_carry_out, add_8_2_carry_out, add_8_3_carry_out;
  wire [31:0] bit_converter_1_to_32_1_out_2, xor_1_out;

  Bit_Converter_1_to_32 bit_converter_1_to_32_1 (.in_1(SUB), .out_2(bit_converter_1_to_32_1_out_2));
  assign xor_1_out = bit_converter_1_to_32_1_out_2 ^ B;  // XOR_Gate xor_1, 32 bits wide
  Add_8 add_8_1 (.A(A[7:0]), .B(xor_1_out[7:0]), .Carry_in(SUB), .Carry_Out(add_8_1_carry_out), .Sum(Sum[7:0]));
  Add_8 add_8_2 (
    .A(A[15:8]), .B(xor_1_out[15:8]), .Carry_in(add_8_1_carry_out), .Carry_Out(add_8_2_carry_out),
    .Sum(Sum[15:8]));
  Add_8 add_8_3 (
    .A(A[23:16]), .B(xor_1_out[23:16]), .Carry_in(add_8_2_carry_out), .Carry_Out(add_8_3_carry_out),
    .Sum(Sum[23:16]));
  Add_8 add_8_4 (
    .A(A[31:24]), .B(xor_1_out[31:24]), .Carry_in(add_8_3_carry_out), .Carry_Out(Carry_Out), .Sum(Sum[31:24]));
endmodule

module Bit_Converter_1_to_32 (
  input  in_1,
  output [31:0] out_2
);


  assign out_2 = {32{in_1}};
endmodule

module Count (
  input  Reset,
  input  clk,
  output [23:0] Counter_out
);

  wire not_1_out;
  wire [31:0] add_32_1_sum, controlled_buffer_1_out;
  wire [31:24] register_32bit_1_out_3;

  Add_32 add_32_1 (.A({register_32bit_1_out_3, Counter_out}), .B(32'h1), .Sum(add_32_1_sum));  // open: SUB, Carry_Out
  not not_1 (not_1_out, Reset);
  assign controlled_buffer_1_out = not_1_out ? add_32_1_sum : 32'bz;  // Controlled_Buffer controlled_buffer_1
  Register_32Bit register_32bit_1 (
    .Data_in(controlled_buffer_1_out), .Set(clk), .out_3({register_32bit_1_out_3, Counter_out}));
endmodule

module Writer (
  input  [31:0] Data_in,
  input  [2:0] Decode,
  output [6:0] Data_out
);

  Multiplexer #(.select(3), .width(7)) multiplexer_1 (
    .in0(Data_in[6:0]), .in1({3'b011, Data_in[3:0]}), .out(Data_out), .sel(Decode));  // open: in2, in3, in4, in5, in6, in7

  // Other names for the same wires on the sheet: DIN[31:0] = Data_in
endmodule
